# Fritzing sketch MatrixGame_Fritzing (saved by Fritzing 0.9.3b)
breadboards: 4

parts:
  LCD = LCD screen
  8x8_Matrix_Display_1088AS = LBT2088AH [part_number=LBT2088AH]
  Driver_MAX7219 = MAX7219 [package=dil24]
  Ceramic_Capacitor_104_pF = Capacitor [package=cap-pth-large]
  R1 = Resistor [tolerance=±5% resistance=220 package=THT]
  Bazzer = Piezo Speaker
  Joystick = Thumb Joystick
  R3 = Resistor [tolerance=±5% resistance=220 package=THT]
  Arduino_Uno = Arduino Uno (Rev3)
  R_-_Resistor_EC_-_Electrolityc_Capacitor_CC_-_Ceramic_Capacitor = Capacitor Polarized [package=cpol-radial-100uf-25v]
  Resistor_10k = Resistor [tolerance=±5% resistance=220 package=THT]

nets:
  GND: LCD.VSS, LCD.RS, LCD.LED-, Driver_MAX7219.GND, Driver_MAX7219.GND2, Ceramic_Capacitor_104_pF.1, Joystick.GND, R3.Pin_0, Arduino_Uno.GND, R_-_Resistor_EC_-_Electrolityc_Capacitor_CC_-_Ceramic_Capacitor.-
  VDD: LCD.VDD, Driver_MAX7219.VCC, Ceramic_Capacitor_104_pF.2, R1.Pin_1, Joystick.SEL, Arduino_Uno.5V, R_-_Resistor_EC_-_Electrolityc_Capacitor_CC_-_Ceramic_Capacitor.+, Resistor_10k.Pin_0
  N1: LCD.V0, Arduino_Uno.D3_PWM
  N2: LCD.R/W, Arduino_Uno.D4
  N3: LCD.E, Arduino_Uno.D5_PWM
  N4: LCD.DB4, Arduino_Uno.D6_PWM
  N5: LCD.DB5, Arduino_Uno.D7
  N6: LCD.DB6, Arduino_Uno.D8
  N7: LCD.DB7, Arduino_Uno.D9_PWM
  N8: LCD.LED+, Resistor_10k.Pin_1
  N9: 8x8_Matrix_Display_1088AS.pin1, Driver_MAX7219.DIG0
  N10: 8x8_Matrix_Display_1088AS.pin2, Driver_MAX7219.SEGC
  N11: 8x8_Matrix_Display_1088AS.pin_3, Driver_MAX7219.SEGE
  N12: 8x8_Matrix_Display_1088AS.pin_4, Driver_MAX7219.DIG3
  N13: 8x8_Matrix_Display_1088AS.pin_5, Driver_MAX7219.SEGDP
  N14: 8x8_Matrix_Display_1088AS.pin_6, Driver_MAX7219.DIG1
  N15: 8x8_Matrix_Display_1088AS.pin_7, Driver_MAX7219.SEGF
  N16: 8x8_Matrix_Display_1088AS.pin_8, Driver_MAX7219.SEGG
  N17: 8x8_Matrix_Display_1088AS.pin_9, Driver_MAX7219.DIG4
  N18: 8x8_Matrix_Display_1088AS.pin_10, Driver_MAX7219.DIG6
  N19: 8x8_Matrix_Display_1088AS.pin_11, Driver_MAX7219.SEGD
  N20: 8x8_Matrix_Display_1088AS.pin_12, Driver_MAX7219.SEGB
  N21: 8x8_Matrix_Display_1088AS.pin_13, Driver_MAX7219.DIG7
  N22: 8x8_Matrix_Display_1088AS.pin_14, Driver_MAX7219.SEGA
  N23: 8x8_Matrix_Display_1088AS.pin_15, Driver_MAX7219.DIG5
  N24: 8x8_Matrix_Display_1088AS.pin_16, Driver_MAX7219.DIG2
  N25: Driver_MAX7219.DIN, Arduino_Uno.D12/MISO
  N26: Driver_MAX7219.LOAD, Arduino_Uno.D10_PWM/SS
  N27: Driver_MAX7219.CLK, Arduino_Uno.D11_PWM/MOSI
  N28: Driver_MAX7219.ISET, R1.Pin_0
  N29: Bazzer.pin1, R3.Pin_1
  N30: Bazzer.pin2, Arduino_Uno.D13/SCK
  N31: Joystick.HORZ, Arduino_Uno.A0
  N32: Joystick.VERT, Arduino_Uno.A1
  N33: Joystick.VCC, Arduino_Uno.D2

notes:
  R 10k Ω
  R 220 Ω
  EC 100nF
  CC 104pF
  R 100 Ω
  1
  8
  9
  16
